// Logisim project EvanDietrich_KevinPak_proj1.circ as structural Verilog: 10 circuits, main circuit fullAdder
module Arch (
  input  [7:0] A,
  input  [7:0] B,
  input  [2:0] opcode,
  output [7:0] O
);

  ALU alu_1 (.A(A), .B(B), .opcode(opcode), .O(O));  // open: cout
endmodule

module ALU (
  input  [7:0] A,
  input  [7:0] B,
  input  [2:0] opcode,
  output [7:0] O,
  output cout
);

  wire eightbitadder_1_cout, eightbitsubtractor_1_carryout;
  wire [7:0] bitwiseand_1_cout, bitwiseor_1_cout, bitwisexor_1_cout, eightbitadder_1_sum,
       eightbitmultiplier_1_mainoutput, eightbitsubtractor_1_diff, logicalshift_1_mainoutput;

  bitwiseXor bitwisexor_1 (.Ain(A), .Bin(B), .Cout(bitwisexor_1_cout));
  bitwiseAnd bitwiseand_1 (.Ain(A), .Bin(B), .Cout(bitwiseand_1_cout));
  bitwiseOR bitwiseor_1 (.Ain(A), .Bin(B), .Cout(bitwiseor_1_cout));
  eightBitAdder eightbitadder_1 (.Ain(A), .Bin(B), .Sum(eightbitadder_1_sum), .Cout(eightbitadder_1_cout));
  eightBitSubtractor eightbitsubtractor_1 (
    .A(A), .B(B), .Diff(eightbitsubtractor_1_diff), .Carryout(eightbitsubtractor_1_carryout));
  LogicalShift logicalshift_1 (.Bin(B), .mainOutput(logicalshift_1_mainoutput));  // open: discard
  eightBitMultiplier eightbitmultiplier_1 (.A(A), .B(B), .mainOutput(eightbitmultiplier_1_mainoutput));
  Multiplexer #(.select(3), .width(8)) multiplexer_1 (
    .in0(B), .in1(bitwisexor_1_cout), .in2(bitwiseand_1_cout), .in3(bitwiseor_1_cout),
    .in4(eightbitadder_1_sum), .in5(eightbitsubtractor_1_diff), .in6(logicalshift_1_mainoutput),
    .in7(eightbitmultiplier_1_mainoutput), .out(O), .sel(opcode));
  or or_1 (cout, eightbitadder_1_cout, eightbitsubtractor_1_carryout);
endmodule

module fullAdder (
  input  A,
  input  B,
  input  Cin,
  output Sum,
  output Cout
);

  wire and_1_out, and_2_out, xor_1_out;

  xor xor_1 (xor_1_out, A, B);
  xor xor_2 (Sum, xor_1_out, Cin);
  and and_1 (and_1_out, xor_1_out, Cin);
  and and_2 (and_2_out, A, B);
  or or_1 (Cout, and_1_out, and_2_out);
endmodule

module eightBitAdder (
  input  [7:0] Ain,
  input  [7:0] Bin,
  output [7:0] Sum,
  output Cout
);

  wire fulladder_1_cout, fulladder_2_cout, fulladder_3_cout, fulladder_4_cout, fulladder_5_cout,
       fulladder_6_cout, fulladder_7_cout;

  fullAdder fulladder_1 (.A(Ain[0]), .B(Bin[0]), .Sum(Sum[0]), .Cout(fulladder_1_cout));  // open: Cin
  fullAdder fulladder_2 (.A(Ain[1]), .B(Bin[1]), .Cin(fulladder_1_cout), .Sum(Sum[1]), .Cout(fulladder_2_cout));
  fullAdder fulladder_3 (.A(Ain[2]), .B(Bin[2]), .Cin(fulladder_2_cout), .Sum(Sum[2]), .Cout(fulladder_3_cout));
  fullAdder fulladder_4 (.A(Ain[3]), .B(Bin[3]), .Cin(fulladder_3_cout), .Sum(Sum[3]), .Cout(fulladder_4_cout));
  fullAdder fulladder_5 (.A(Ain[4]), .B(Bin[4]), .Cin(fulladder_4_cout), .Sum(Sum[4]), .Cout(fulladder_5_cout));
  fullAdder fulladder_6 (.A(Ain[5]), .B(Bin[5]), .Cin(fulladder_5_cout), .Sum(Sum[5]), .Cout(fulladder_6_cout));
  fullAdder fulladder_7 (.A(Ain[6]), .B(Bin[6]), .Cin(fulladder_6_cout), .Sum(Sum[6]), .Cout(fulladder_7_cout));
  fullAdder fulladder_8 (.A(Ain[7]), .B(Bin[7]), .Cin(fulladder_7_cout), .Sum(Sum[7]), .Cout(Cout));
endmodule

module bitwiseXor (
  input  [7:0] Ain,
  input  [7:0] Bin,
  output [7:0] Cout
);

  xor xor_1 (Cout[0], Ain[0], Bin[0]);
  xor xor_2 (Cout[1], Ain[1], Bin[1]);
  xor xor_3 (Cout[2], Ain[2], Bin[2]);
  xor xor_4 (Cout[3], Ain[3], Bin[3]);
  xor xor_5 (Cout[4], Ain[4], Bin[4]);
  xor xor_6 (Cout[5], Ain[5], Bin[5]);
  xor xor_7 (Cout[6], Ain[6], Bin[6]);
  xor xor_8 (Cout[7], Ain[7], Bin[7]);
endmodule

module bitwiseAnd (
  input  [7:0] Ain,
  input  [7:0] Bin,
  output [7:0] Cout
);

  and and_1 (Cout[0], Ain[0], Bin[0]);
  and and_2 (Cout[1], Ain[1], Bin[1]);
  and and_3 (Cout[2], Ain[2], Bin[2]);
  and and_4 (Cout[3], Ain[3], Bin[3]);
  and and_5 (Cout[4], Ain[4], Bin[4]);
  and and_6 (Cout[5], Ain[5], Bin[5]);
  and and_7 (Cout[6], Ain[6], Bin[6]);
  and and_8 (Cout[7], Ain[7], Bin[7]);
endmodule

module bitwiseOR (
  input  [7:0] Ain,
  input  [7:0] Bin,
  output [7:0] Cout
);

  or or_1 (Cout[0], Ain[0], Bin[0]);
  or or_2 (Cout[1], Ain[1], Bin[1]);
  or or_3 (Cout[2], Ain[2], Bin[2]);
  or or_4 (Cout[3], Ain[3], Bin[3]);
  or or_5 (Cout[4], Ain[4], Bin[4]);
  or or_6 (Cout[5], Ain[5], Bin[5]);
  or or_7 (Cout[6], Ain[6], Bin[6]);
  or or_8 (Cout[7], Ain[7], Bin[7]);
endmodule

module eightBitSubtractor (
  input  [7:0] A,
  input  [7:0] B,
  output [7:0] Diff,
  output Carryout
);

  wire fulladder_1_cout, fulladder_2_cout, fulladder_3_cout, fulladder_4_cout, fulladder_5_cout,
       fulladder_6_cout, fulladder_7_cout, xor_1_out, xor_2_out, xor_3_out, xor_4_out, xor_5_out, xor_6_out,
       xor_7_out, xor_8_out;

  xor xor_1 (xor_1_out, B[0], 1'b1);
  xor xor_2 (xor_2_out, B[1], 1'b1);
  xor xor_3 (xor_3_out, B[2], 1'b1);
  xor xor_4 (xor_4_out, B[3], 1'b1);
  xor xor_5 (xor_5_out, B[4], 1'b1);
  xor xor_6 (xor_6_out, B[5], 1'b1);
  xor xor_7 (xor_7_out, A[4], 1'b1);
  xor xor_8 (xor_8_out, B[7], 1'b1);
  fullAdder fulladder_1 (.A(A[0]), .B(xor_1_out), .Cin(1'b1), .Sum(Diff[0]), .Cout(fulladder_1_cout));
  fullAdder fulladder_2 (.A(A[1]), .B(xor_2_out), .Cin(fulladder_1_cout), .Sum(Diff[1]), .Cout(fulladder_2_cout));
  fullAdder fulladder_3 (.A(A[2]), .B(xor_3_out), .Cin(fulladder_2_cout), .Sum(Diff[2]), .Cout(fulladder_3_cout));
  fullAdder fulladder_4 (.A(A[3]), .B(xor_4_out), .Cin(fulladder_3_cout), .Sum(Diff[3]), .Cout(fulladder_4_cout));
  fullAdder fulladder_5 (.A(A[4]), .B(xor_5_out), .Cin(fulladder_4_cout), .Sum(Diff[4]), .Cout(fulladder_5_cout));
  fullAdder fulladder_6 (.A(A[5]), .B(xor_6_out), .Cin(fulladder_5_cout), .Sum(Diff[5]), .Cout(fulladder_6_cout));
  fullAdder fulladder_7 (.A(A[6]), .B(xor_7_out), .Cin(fulladder_6_cout), .Sum(Diff[6]), .Cout(fulladder_7_cout));
  fullAdder fulladder_8 (.A(A[7]), .B(xor_8_out), .Cin(fulladder_7_cout), .Sum(Diff[7]), .Cout(Carryout));

  assign B[6] = A[4];
endmodule

module eightBitMultiplier (
  input  [7:0] A,
  input  [7:0] B,
  output [7:0] mainOutput
);

  wire [2:0] and_15_out;
  wire [3:0] and_5_out, and_8_out, and_12_out;
  wire [3:1] adder_1_out, adder_2_out;
  wire [3:3] adder_1_cout, adder_2_cout;

  and and_1 (and_5_out[3], B[3], A[3]);
  and and_2 (and_5_out[2], B[3], A[2]);
  and and_3 (and_5_out[1], B[3], A[1]);
  and and_4 (and_8_out[3], B[2], A[3]);
  and and_5 (and_5_out[0], B[3], A[0]);
  and and_6 (and_8_out[2], B[2], A[2]);
  and and_7 (and_8_out[1], B[2], A[1]);
  and and_8 (and_8_out[0], B[2], A[0]);
  and and_9 (and_12_out[3], B[1], A[3]);
  and and_10 (and_12_out[2], B[1], A[2]);
  and and_11 (and_12_out[1], B[1], A[1]);
  and and_12 (and_12_out[0], B[1], A[0]);
  and and_13 (and_15_out[2], B[0], A[3]);
  and and_14 (and_15_out[1], B[0], A[2]);
  and and_15 (and_15_out[0], B[0], A[1]);
  and and_16 (mainOutput[0], B[0], A[0]);
  Adder #(.width(4)) adder_1 (
    .a({1'b0, and_15_out}), .b(and_12_out), .out({adder_1_out, mainOutput[1]}), .cin(1'b0),
    .cout(adder_1_cout[3]));
  Adder #(.width(4)) adder_2 (
    .a({adder_1_cout[3], adder_1_out}), .b(and_8_out), .out({adder_2_out, mainOutput[2]}), .cin(1'b0),
    .cout(adder_2_cout[3]));
  Adder #(.width(4)) adder_3 (
    .a({adder_2_cout[3], adder_2_out}), .b(and_5_out), .out(mainOutput[6:3]), .cin(1'b0), .cout(mainOutput[7]));
endmodule

module LogicalShift (
  input  [7:0] Bin,
  output discard,
  output [7:0] mainOutput
);


  assign discard = Bin[0];
  assign mainOutput = {1'b0, Bin[7:1]};
endmodule
